# Fritzing sketch IoT based Automatic Trash Bin with Capacity Indicator (saved by Fritzing 0.9.2b)
breadboards: 1

parts:
  U1 = ESP32-38PinWide [part_number=ESP32-38PinWide]
  Part2 = HC-SR04
  Part3 = HC-SR04
  J1 = Basic Servo
  Part4 = LCD1602-I2C

nets:
  N1: U1.GPIO32, Part2.Echo
  N2: U1.GPIO33, Part2.Trig
  N3: U1.GPIO26, Part3.Echo
  N4: U1.GPIO27, Part3.Trig
  N5: U1.GPIO13, J1.pulse
  GND: U1.GPIO11, Part2.Gnd, Part3.Gnd, J1.gnd, Part4.GND
  VCC: U1.VIN, Part2.Vcc, Part3.Vcc, J1.vcc, Part4.VCC
  N6: U1.GPIO21, Part4.SDA
  N7: U1.GPIO22, Part4.SCL

custom parts:
  ESP32-38PinWide: Generic 38-Pin ESP32 with wide format (only access to one side of pins on a breadboard) based on Stephen Lilley's HiLetgo ESP-WROOM-32 ESP32 ESP-32S Development Board.
  HC-SR04: HC-SR04 ultrasonic distance sensor
  LCD1602-I2C: A standard character display, usually with 2x16 characters. Comes in many colors with LCM1602 IIC attached.
